# Fritzing sketch USB-Timer 3 (saved by Fritzing 0.9.6b)

parts:
  WeMos_D1_Mini1 = WeMos D1 Mini
  Q1 = MOSFET-NCHANNEL [package=to220v]
  R1 = Resistor [tolerance=±5% power=0.25 resistance=220 package=THT]
  X2 = USB Connectors [package=usb-a-s-silk-female]
  JP1 = USB_MICROB_PLUG [package=micro-b-th]

nets:
  N1: WeMos_D1_Mini1.D5, Q1.G, R1.Pin_0
  N2: WeMos_D1_Mini1.G, Q1.S, R1.Pin_1, JP1.GND
  N3: Q1.D, X2.GND
  N4: X2.D+, JP1.D+
  N5: X2.D-, JP1.D-
  N6: X2.VBUS, JP1.VCC
